# Fritzing sketch TrafficLightDemo (saved by Fritzing 0.9.2b)
circuit board: 7.2445cm x 5.67518cm
breadboards: 1

parts:
  Part1 = Arduino Uno (Rev3)
  LED2 = LED - 5mm [color="Yellow (585nm)" package="5 mm [THT]"]
  LED3 = LED - 5mm [color="Green (555nm)" package="5 mm [THT]"]
  R2 = Resistor [tolerance=±5% resistance=100 package=THT]
  R3 = Resistor [tolerance=±5% resistance=100 package=THT]
  LED1 = LED - 5mm [color="Red (635nm)" package="5 mm [THT]"]
  R4 = Resistor [tolerance=±5% resistance=100 package=THT]
  R5 = Resistor [tolerance=±5% resistance=100 package=THT]
  LED6 = LED - 5mm [color="Green (555nm)" package="5 mm [THT]"]
  LED5 = LED - 5mm [color="Yellow (585nm)" package="5 mm [THT]"]
  LED4 = LED - 5mm [color="Red (635nm)" package="5 mm [THT]"]
  R1 = Resistor [tolerance=±5% resistance=100 package=THT]
  R6 = Resistor [tolerance=±5% resistance=100 package=THT]
  V1 = DC Power [voltage=5V]

nets:
  N1: Part1.D10_PWM/SS, LED6.anode
  N2: Part1.D11_PWM/MOSI, LED5.anode
  N3: Part1.D12/MISO, LED4.anode
  GND: Part1.GND, R2.Pin_1, R3.Pin_1, R4.Pin_1, R5.Pin_1, R1.Pin_1, R6.Pin_1, V1.V-
  N4: Part1.D3_PWM, LED3.anode
  N5: Part1.D4, LED2.anode
  N6: Part1.D5_PWM, LED1.anode
  N7: Part1.5V, V1.V+
  N8: LED2.cathode, R2.Pin_0
  N9: LED3.cathode, R3.Pin_0
  N10: LED1.cathode, R1.Pin_0
  N11: R4.Pin_0, LED4.cathode
  N12: R5.Pin_0, LED5.cathode
  N13: LED6.cathode, R6.Pin_0
